// Logisim project saguiVLIW.circ as structural Verilog: 6 circuits, main circuit main
module main (
);

  wire clk, controle_1_memread, controle_1_memwrite, controle_2_branch, controle_3_muxula, r01, r02,
       RegWrite1, RegWrite2, RegWrite3, RegWrite4, reset;
  wire [1:0] controle_2_branchtype, multiplexer_2_out, multiplexer_3_out, MuxWrite;
  wire [2:0] controle_3_ulacontrol, controle_4_ulacontrol;
  wire [7:0] bancoregistrador_1_saidaa1, bancoregistrador_1_saidaa2, bancoregistrador_1_saidaa3,
       bancoregistrador_1_saidaa4, bancoregistrador_1_saidab1, bancoregistrador_1_saidab2,
       bancoregistrador_1_saidab3, bancoregistrador_1_saidab4, brjump_1_nextpc, ldstmv_1_mvhight,
       ldstmv_1_mvlow, multiplexer_1_out, multiplexer_4_out, pc, ram_1_dout, ula_1_saida, ula_2_saida;
  wire [31:0] rom_1_data;

  Clock clock_1 (.out(clk));
  Multiplexer #(.width(8)) multiplexer_1 (.in0(brjump_1_nextpc), .in1({8{1'b0}}), .out(multiplexer_1_out), .sel(reset));
  Register register_1 (.D(multiplexer_1_out), .en(1'b1), .clk(clk), .Q(pc), .clr(reset));
  Button button_1 (.out(reset));
  ROM #(.dataWidth(32)) rom_1 (.addr(pc), .data(rom_1_data));
  Multiplexer #(.width(2)) multiplexer_2 (.in0(rom_1_data[11:10]), .in1(2'b00), .out(multiplexer_2_out), .sel(r02));
  Multiplexer #(.width(2)) multiplexer_3 (.in0(rom_1_data[3:2]), .in1(2'b00), .out(multiplexer_3_out), .sel(r01));
  bancoRegistrador bancoregistrador_1 (
    .RegA1(multiplexer_3_out), .RegA2(multiplexer_2_out), .RegA3(rom_1_data[19:18]),
    .RegA4(rom_1_data[27:26]), .RegB1(rom_1_data[1:0]), .RegB2(rom_1_data[9:8]), .RegB3(rom_1_data[17:16]),
    .RegB4(rom_1_data[25:24]), .RegWrite1(RegWrite1), .RegWrite2(RegWrite2), .RegWrite3(RegWrite3),
    .RegWrite4(RegWrite4), .RegValue1(multiplexer_4_out), .RegValue3(ula_1_saida), .RegValue4(ula_2_saida),
    .Reset(reset), .SaidaB1(bancoregistrador_1_saidab1), .SaidaA1(bancoregistrador_1_saidaa1),
    .SaidaA2(bancoregistrador_1_saidaa2), .SaidaB2(bancoregistrador_1_saidab2),
    .SaidaA3(bancoregistrador_1_saidaa3), .SaidaB3(bancoregistrador_1_saidab3),
    .SaidaA4(bancoregistrador_1_saidaa4), .SaidaB4(bancoregistrador_1_saidab4));  // open: RegValue2
  Multiplexer #(.select(2), .width(8)) multiplexer_4 (
    .in0({8{1'b0}}), .in1(ram_1_dout), .in2(ldstmv_1_mvhight), .in3(ldstmv_1_mvlow), .out(multiplexer_4_out),
    .sel(MuxWrite));
  controle controle_1 (
    .in_1(rom_1_data[7:4]), .r0(r01), .MemRead(controle_1_memread), .MemWrite(controle_1_memwrite),
    .RegWrite(RegWrite1), .MuxWrite(MuxWrite));  // open: ULAControl, BranchType, Branch, MuxULA
  controle controle_2 (
    .in_1(rom_1_data[15:12]), .BranchType(controle_2_branchtype), .Branch(controle_2_branch), .r0(r02),
    .RegWrite(RegWrite2));  // open: ULAControl, MemRead, MemWrite, MuxULA, MuxWrite
  controle controle_3 (
    .in_1(rom_1_data[23:20]), .ULAControl(controle_3_ulacontrol), .MuxULA(controle_3_muxula),
    .RegWrite(RegWrite3));  // open: BranchType, Branch, r0, MemRead, MemWrite, MuxWrite
  controle controle_4 (
    .in_1(rom_1_data[31:28]), .ULAControl(controle_4_ulacontrol), .RegWrite(RegWrite4));  // open: BranchType, Branch, r0, MemRead, MemWrite, MuxULA, MuxWrite
  BrJump brjump_1 (
    .BranchType(controle_2_branchtype), .Branch(controle_2_branch), .ra(bancoregistrador_1_saidaa2),
    .rb(bancoregistrador_1_saidab2), .IMM(rom_1_data[11:8]), .PC(pc), .NextPC(brjump_1_nextpc));
  Ula ula_1 (
    .ra(bancoregistrador_1_saidaa3), .rb(bancoregistrador_1_saidab3), .OpULA(controle_3_ulacontrol),
    .saida(ula_1_saida));  // open: zero
  Ula ula_2 (
    .ra(bancoregistrador_1_saidaa4), .rb(bancoregistrador_1_saidab4), .OpULA(controle_4_ulacontrol),
    .saida(ula_2_saida));  // open: zero
  LdStMv ldstmv_1 (
    .ra(bancoregistrador_1_saidaa1), .imm(rom_1_data[3:0]), .MvHight(ldstmv_1_mvhight), .MvLow(ldstmv_1_mvlow));
  RAM #(.trigger("falling")) ram_1 (
    .addr(bancoregistrador_1_saidab1), .we(controle_1_memwrite), .oe(controle_1_memread), .clk(clk),
    .din(bancoregistrador_1_saidaa1), .dout(ram_1_dout));

  // Notes on the sheet:
  //   PC
  //   contents of rom_1 (hex, n*v repeats v):
  //   ffffff61 ffffff51 ffffff72 ffffff4a ff84ffff 92ffffff ffa3ffff b2ffffff ffcbffff d8ffffff ffe2ffff
  //   ffffff60 ff86ffff ffff01ff 20*0 ffffff62 ffffff71 ff94ffff ffffff62 ffffff76 88ffffff ffff22ff 13*0
  //   918d0053 918d2253
  //   instruction memory
  //   imm
  //   1º
  //   2º
  //   imm
  //   3º
  //   ra/rb
  //   ra/rb
  //   ra/rb
endmodule

module bancoRegistrador (
  input  [7:0] RegValue1,
  input  [7:0] RegValue2,
  input  [7:0] RegValue3,
  input  [7:0] RegValue4,
  input  RegWrite1,
  input  RegWrite2,
  input  RegWrite3,
  input  RegWrite4,
  input  Reset,
  input  [1:0] RegA1,
  input  [1:0] RegA2,
  input  [1:0] RegA3,
  input  [1:0] RegA4,
  input  [1:0] RegB1,
  input  [1:0] RegB2,
  input  [1:0] RegB3,
  input  [1:0] RegB4,
  output [7:0] SaidaA1,
  output [7:0] SaidaA2,
  output [7:0] SaidaB1,
  output [7:0] SaidaB2,
  output [7:0] SaidaA3,
  output [7:0] SaidaB3,
  output [7:0] SaidaA4,
  output [7:0] SaidaB4
);

  wire clk, demultiplexer_1_out0, demultiplexer_1_out1, demultiplexer_1_out2, demultiplexer_1_out3,
       demultiplexer_2_out0, demultiplexer_2_out1, demultiplexer_2_out2, demultiplexer_2_out3,
       demultiplexer_3_out0, demultiplexer_3_out1, demultiplexer_3_out2, demultiplexer_3_out3,
       demultiplexer_4_out0, demultiplexer_4_out1, demultiplexer_4_out2, demultiplexer_4_out3, or_1_out,
       or_2_out, or_3_out, or_4_out;
  wire [1:0] demultiplexer_5_out0, demultiplexer_5_out1, demultiplexer_5_out2, demultiplexer_5_out3,
       demultiplexer_6_out0, demultiplexer_6_out1, demultiplexer_6_out2, demultiplexer_6_out3,
       demultiplexer_7_out0, demultiplexer_7_out1, demultiplexer_7_out2, demultiplexer_7_out3,
       demultiplexer_8_out0, demultiplexer_8_out1, demultiplexer_8_out2, demultiplexer_8_out3,
       multiplexer_1_out, multiplexer_2_out, multiplexer_3_out, multiplexer_4_out, r0, r1, r2, r3;
  wire [7:0] multiplexer_5_out, multiplexer_6_out, multiplexer_7_out, multiplexer_8_out, r0_q, r1_q, r2_q,
       r3_q;

  Multiplexer #(.width(2)) multiplexer_1 (.in0(2'b00), .in1(2'b00), .out(multiplexer_1_out), .sel(RegWrite1));
  Multiplexer #(.width(2)) multiplexer_2 (.in0(2'b00), .in1(2'b01), .out(multiplexer_2_out), .sel(RegWrite2));
  Multiplexer #(.width(2)) multiplexer_3 (.in0(2'b00), .in1(2'b10), .out(multiplexer_3_out), .sel(RegWrite3));
  Multiplexer #(.width(2)) multiplexer_4 (.in0(2'b00), .in1(2'b11), .out(multiplexer_4_out), .sel(RegWrite4));
  Demultiplexer #(.select(2)) demultiplexer_1 (
    .out0(demultiplexer_1_out0), .out1(demultiplexer_1_out1), .out2(demultiplexer_1_out2),
    .out3(demultiplexer_1_out3), .in(RegWrite1), .sel(RegA1));
  Demultiplexer #(.select(2)) demultiplexer_2 (
    .out0(demultiplexer_2_out0), .out1(demultiplexer_2_out1), .out2(demultiplexer_2_out2),
    .out3(demultiplexer_2_out3), .in(RegWrite2), .sel(RegA2));
  Demultiplexer #(.select(2)) demultiplexer_3 (
    .out0(demultiplexer_3_out0), .out1(demultiplexer_3_out1), .out2(demultiplexer_3_out2),
    .out3(demultiplexer_3_out3), .in(RegWrite3), .sel(RegA3));
  Demultiplexer #(.select(2)) demultiplexer_4 (
    .out0(demultiplexer_4_out0), .out1(demultiplexer_4_out1), .out2(demultiplexer_4_out2),
    .out3(demultiplexer_4_out3), .in(RegWrite4), .sel(RegA4));
  Demultiplexer #(.select(2), .width(2)) demultiplexer_5 (
    .out0(demultiplexer_5_out0), .out1(demultiplexer_5_out1), .out2(demultiplexer_5_out2),
    .out3(demultiplexer_5_out3), .in(multiplexer_1_out), .sel(RegA1));
  Demultiplexer #(.select(2), .width(2)) demultiplexer_6 (
    .out0(demultiplexer_6_out0), .out1(demultiplexer_6_out1), .out2(demultiplexer_6_out2),
    .out3(demultiplexer_6_out3), .in(multiplexer_2_out), .sel(RegA2));
  Demultiplexer #(.select(2), .width(2)) demultiplexer_7 (
    .out0(demultiplexer_7_out0), .out1(demultiplexer_7_out1), .out2(demultiplexer_7_out2),
    .out3(demultiplexer_7_out3), .in(multiplexer_3_out), .sel(RegA3));
  Demultiplexer #(.select(2), .width(2)) demultiplexer_8 (
    .out0(demultiplexer_8_out0), .out1(demultiplexer_8_out1), .out2(demultiplexer_8_out2),
    .out3(demultiplexer_8_out3), .in(multiplexer_4_out), .sel(RegA4));
  or or_1 (or_1_out, demultiplexer_1_out0, demultiplexer_2_out0, demultiplexer_3_out0, demultiplexer_4_out0);
  or or_2 (or_2_out, demultiplexer_1_out1, demultiplexer_2_out1, demultiplexer_3_out1, demultiplexer_4_out1);
  or or_3 (or_3_out, demultiplexer_1_out2, demultiplexer_2_out2, demultiplexer_3_out2, demultiplexer_4_out2);
  or or_4 (or_4_out, demultiplexer_1_out3, demultiplexer_2_out3, demultiplexer_3_out3, demultiplexer_4_out3);
  assign r0 = demultiplexer_5_out0 | demultiplexer_6_out0 | demultiplexer_7_out0 | demultiplexer_8_out0;  // OR_Gate or_5, 2 bits wide
  Register u_r0 (.D(multiplexer_5_out), .en(or_1_out), .clk(clk), .Q(r0_q), .clr(Reset));
  Multiplexer #(.select(2), .width(8)) multiplexer_5 (
    .in0(RegValue1), .in1(RegValue2), .in2(RegValue3), .in3(RegValue4), .out(multiplexer_5_out), .sel(r0));
  Multiplexer #(.select(2), .width(8)) multiplexer_6 (
    .in0(RegValue1), .in1(RegValue2), .in2(RegValue3), .in3(RegValue4), .out(multiplexer_6_out), .sel(r1));
  Register u_r1 (.D(multiplexer_6_out), .en(or_2_out), .clk(clk), .Q(r1_q), .clr(Reset));
  assign r1 = demultiplexer_5_out1 | demultiplexer_6_out1 | demultiplexer_7_out1 | demultiplexer_8_out1;  // OR_Gate or_6, 2 bits wide
  assign r2 = demultiplexer_5_out2 | demultiplexer_6_out2 | demultiplexer_7_out2 | demultiplexer_8_out2;  // OR_Gate or_7, 2 bits wide
  assign r3 = demultiplexer_5_out3 | demultiplexer_6_out3 | demultiplexer_7_out3 | demultiplexer_8_out3;  // OR_Gate or_8, 2 bits wide
  Register u_r2 (.D(multiplexer_7_out), .en(or_3_out), .clk(clk), .Q(r2_q), .clr(Reset));
  Multiplexer #(.select(2), .width(8)) multiplexer_7 (
    .in0(RegValue1), .in1(RegValue2), .in2(RegValue3), .in3(RegValue4), .out(multiplexer_7_out), .sel(r2));
  Register u_r3 (.D(multiplexer_8_out), .en(or_4_out), .clk(clk), .Q(r3_q), .clr(Reset));
  Multiplexer #(.select(2), .width(8)) multiplexer_8 (
    .in0(RegValue1), .in1(RegValue2), .in2(RegValue3), .in3(RegValue4), .out(multiplexer_8_out), .sel(r3));
  Clock clock_1 (.out(clk));
  Multiplexer #(.select(2), .width(8)) multiplexer_9 (
    .in0(r0_q), .in1(r1_q), .in2(r2_q), .in3(r3_q), .out(SaidaA1), .sel(RegA1));
  Multiplexer #(.select(2), .width(8)) multiplexer_10 (
    .in0(r0_q), .in1(r1_q), .in2(r2_q), .in3(r3_q), .out(SaidaA2), .sel(RegA2));
  Multiplexer #(.select(2), .width(8)) multiplexer_11 (
    .in0(r0_q), .in1(r1_q), .in2(r2_q), .in3(r3_q), .out(SaidaB1), .sel(RegB1));
  Multiplexer #(.select(2), .width(8)) multiplexer_12 (
    .in0(r0_q), .in1(r1_q), .in2(r2_q), .in3(r3_q), .out(SaidaB2), .sel(RegB2));
  Multiplexer #(.select(2), .width(8)) multiplexer_13 (
    .in0(r0_q), .in1(r1_q), .in2(r2_q), .in3(r3_q), .out(SaidaA3), .sel(RegA3));
  Multiplexer #(.select(2), .width(8)) multiplexer_14 (
    .in0(r0_q), .in1(r1_q), .in2(r2_q), .in3(r3_q), .out(SaidaB3), .sel(RegB3));
  Multiplexer #(.select(2), .width(8)) multiplexer_15 (
    .in0(r0_q), .in1(r1_q), .in2(r2_q), .in3(r3_q), .out(SaidaA4), .sel(RegA4));
  Multiplexer #(.select(2), .width(8)) multiplexer_16 (
    .in0(r0_q), .in1(r1_q), .in2(r2_q), .in3(r3_q), .out(SaidaB4), .sel(RegB4));
endmodule

module Ula (
  input  [7:0] ra,
  input  [7:0] rb,
  input  [2:0] OpULA,
  output zero,
  output [7:0] saida
);

  wire [2:0] bit_extender_1_out;
  wire [7:0] adder_1_out, and_1_out, not_1_out, or_1_out, shifter_1_out, shifter_2_out, subtractor_1_out;

  Bit_Extender #(.out_width(3)) bit_extender_1 (.in(rb), .out(bit_extender_1_out));
  assign not_1_out = ~rb;  // NOT_Gate not_1, 8 bits wide
  Adder adder_1 (.a(ra), .b(rb), .out(adder_1_out));  // open: cin, cout
  Subtractor subtractor_1 (.a(ra), .b(rb), .out(subtractor_1_out));  // open: bin, bout
  assign and_1_out = ra & rb;  // AND_Gate and_1, 8 bits wide
  assign or_1_out = ra | rb;  // OR_Gate or_1, 8 bits wide
  Shifter shifter_1 (.in(rb), .\dist (bit_extender_1_out), .out(shifter_1_out));
  Shifter #(.shift("lr")) shifter_2 (.in(rb), .\dist (bit_extender_1_out), .out(shifter_2_out));
  Multiplexer #(.select(3), .width(8)) multiplexer_1 (
    .in0(adder_1_out), .in1(subtractor_1_out), .in2(and_1_out), .in3(or_1_out), .in4(not_1_out),
    .in5(shifter_1_out), .in6(shifter_2_out), .out(saida), .sel(OpULA));  // open: in7
  Comparator comparator_1 (.a({8{1'b0}}), .b(saida), .eq(zero));  // open: gt, lt
endmodule

module controle (
  input  [3:0] in_1,
  output [2:0] ULAControl,
  output [1:0] BranchType,
  output Branch,
  output r0,
  output MemRead,
  output MemWrite,
  output [1:0] MuxWrite,
  output MuxULA,
  output RegWrite
);

  wire [15:13] controle_data;

  ROM #(.addrWidth(4), .dataWidth(16)) controle (
    .addr(in_1),
    .data({controle_data, RegWrite, MuxULA, MuxWrite, MemWrite, MemRead, r0, Branch, BranchType, ULAControl}));

  // Notes on the sheet:
  //   contents of controle (hex, n*v repeats v):
  //   821 869 831 839 1280 100 1440 1640 1000 1001 1002 1003 1004 1005 1006
  //   controle
endmodule

module BrJump (
  input  [1:0] BranchType,
  input  Branch,
  input  [7:0] ra,
  input  [7:0] rb,
  input  [3:0] IMM,
  input  [7:0] PC,
  output [7:0] NextPC
);

  wire comparator_1_eq;
  wire [7:0] adder_1_out, adder_2_out, bit_extender_1_out, multiplexer_2_out, multiplexer_3_out,
       multiplexer_4_out;

  Multiplexer #(.width(8)) multiplexer_1 (.in0(adder_1_out), .in1(multiplexer_2_out), .out(NextPC), .sel(Branch));
  Multiplexer #(.select(2), .width(8)) multiplexer_2 (
    .in0(multiplexer_3_out), .in1(multiplexer_4_out), .in2(rb), .in3(adder_2_out), .out(multiplexer_2_out),
    .sel(BranchType));
  Adder adder_1 (.a(8'h1), .b(PC), .out(adder_1_out));  // open: cin, cout
  Multiplexer #(.width(8)) multiplexer_3 (.in0(adder_1_out), .in1(rb), .out(multiplexer_3_out), .sel(comparator_1_eq));
  Multiplexer #(.width(8)) multiplexer_4 (
    .in0(adder_1_out), .in1(adder_2_out), .out(multiplexer_4_out), .sel(comparator_1_eq));
  Adder adder_2 (.a(PC), .b(bit_extender_1_out), .out(adder_2_out));  // open: cin, cout
  assign bit_extender_1_out = {{4{IMM[3]}}, IMM};  // Bit_Extender bit_extender_1
  Comparator comparator_1 (.a({8{1'b0}}), .b(ra), .eq(comparator_1_eq));  // open: gt, lt

  // Notes on the sheet:
  //   brzr
  //   brzi
  //   jr
  //   ji
endmodule

module LdStMv (
  input  [7:0] ra,
  input  [3:0] imm,
  output [7:0] MvHight,
  output [7:0] MvLow
);


  assign MvHight = {imm, ra[3:0]};
  assign MvLow = {ra[7:4], imm};

  // Notes on the sheet:
  //   mvHight
  //   mvLow
endmodule
